// Logisim project Lab9.circ as structural Verilog
module C_SR_latch (
  input  R,
  input  C,
  input  S,
  output Qbar,
  output Q
);

  wire nand_1_out, nand_2_out;

  nand nand_1 (nand_1_out, R, C);
  nand nand_2 (nand_2_out, C, S);
  nand nand_3 (Qbar, nand_1_out, Q);
  nand nand_4 (Q, Qbar, nand_2_out);
endmodule

module SR_latch (
  input  R,
  input  S,
  output Q,
  output Qbar
);

  nor nor_1 (Q, R, Qbar);
  nor nor_2 (Qbar, Q, S);
endmodule

module C_D_latch (
  input  D,
  input  C,
  output Qbar,
  output Q
);

  wire nand_1_out, nand_2_out, not_1_out;

  not not_1 (not_1_out, D);
  nand nand_1 (nand_1_out, not_1_out, C);
  nand nand_2 (nand_2_out, C, D);
  nand nand_3 (Qbar, nand_1_out, Q);
  nand nand_4 (Q, Qbar, nand_2_out);
endmodule

module ET_D_flip_flop (
  input  D,
  input  clk,
  output Qbar,
  output Q
);

  wire master_latch_q, not_1_out;

  not not_1 (not_1_out, clk);
  C_D_latch master_latch (.D(D), .C(not_1_out), .Q(master_latch_q));  // open: Qbar
  C_D_latch slave_latch (.D(master_latch_q), .C(clk), .Qbar(Qbar), .Q(Q));
endmodule

module MS_SR_flip_flop (
  input  R,
  input  C,
  input  S,
  output Qbar,
  output Q
);

  wire c_sr_latch_1_q, c_sr_latch_1_qbar, not_1_out, not_2_out;

  not not_1 (not_1_out, C);
  not not_2 (not_2_out, not_1_out);
  C_SR_latch c_sr_latch_1 (.R(R), .C(not_1_out), .S(S), .Qbar(c_sr_latch_1_qbar), .Q(c_sr_latch_1_q));
  C_SR_latch c_sr_latch_2 (.R(c_sr_latch_1_qbar), .C(not_2_out), .S(c_sr_latch_1_q), .Qbar(Qbar), .Q(Q));
endmodule
