// Logisim project LabA.circ as structural Verilog
module FD (
  input  D,
  input  clk,
  output Q,
  output Qn
);
endmodule

module Counter4b (
  input  clk,
  output Qa,
  output Qb,
  output Qc,
  output Qd,
  output Rc
);

  wire and_1_out, and_3_out, and_4_out, and_5_out, and_6_out, FD0_qn, FD1_qn, or_1_out, or_2_out, xor_1_out,
       xor_2_out;

  and and_1 (and_1_out, Qa, Qb, Qc);
  FD FD0 (.D(FD0_qn), .clk(clk), .Q(Qa), .Qn(FD0_qn));
  FD FD1 (.D(or_1_out), .clk(clk), .Q(Qb), .Qn(FD1_qn));
  FD FD2 (.D(or_2_out), .clk(clk), .Q(Qc));  // open: Qn
  FD FD3 (.D(xor_2_out), .clk(clk), .Q(Qd));  // open: Qn
  and and_2 (Rc, Qa, Qb, Qc, Qd);
  and and_3 (and_3_out, FD1_qn, Qc);
  and and_4 (and_4_out, FD0_qn, Qb);
  and and_5 (and_5_out, Qa, FD1_qn);
  or or_1 (or_1_out, and_4_out, and_5_out);
  xor xor_1 (xor_1_out, Qa, Qc);
  and and_6 (and_6_out, xor_1_out, Qb);
  or or_2 (or_2_out, and_6_out, and_3_out);
  xor xor_2 (xor_2_out, and_1_out, Qd);
endmodule
